# Fritzing sketch ArduinoECG (saved by Fritzing 0.9.3b)
breadboards: 1

parts:
  IC1 = AD8232 HeartRate Monitor [part_number=SEN-12650 chip_label=IC package="DIP (Dual Inline) [THT]"]
  Part1 = Arduino Uno (Rev3)
  LCD1 = LCD screen
  LED2 = smd LED [color="Red (633nm)" package="1206 [SMD]"]
  LED3 = LED - 5mm [color="Blue (430nm)" package="5 mm [THT]"]
  R2 = Resistor [tolerance=±5% resistance=220 package="0805 [SMD]"]
  R3 = Resistor [tolerance=±5% resistance=220 package="0805 [SMD]"]

nets:
  GND: IC1.GND, Part1.GND, LCD1.VSS, LED2.cathode, LED3.cathode
  3.3V: IC1.3.3v, Part1.3V3
  N1: IC1.OUTPUT, Part1.A0
  N2: IC1.LO-, Part1.D11_PWM/MOSI
  N3: IC1.LO+, Part1.D10_PWM/SS
  N4: Part1.D12/MISO, R2.Pin_1
  N5: Part1.D13/SCK, R3.Pin_1
  N6: Part1.D2, LCD1.DB0
  N7: Part1.D3_PWM, LCD1.DB1
  N8: Part1.D4, LCD1.DB2
  N9: Part1.D5_PWM, LCD1.DB3
  5V: Part1.5V, LCD1.VDD
  N10: LED2.anode, R3.Pin_0
  N11: LED3.anode, R2.Pin_0

custom parts:
  AD8232 HeartRate Monitor: A DIP stand-in part for whatever IC you want. With 10 pins on a 600mil dual inline package (DIP) footprint.
